# Fritzing sketch bb2636pp0420 (saved by Fritzing 0.9.3b)
circuit board: 10cm x 10cm
breadboards: 1

parts:
  J4 = female pin header, 36 pins [form="♀ (female)"]
  J5 = female pin header, 36 pins [form="♀ (female)"]
  J13 = female pin header, 36 pins [form="♀ (female)"]
  J14 = female pin header, 36 pins [form="♀ (female)"]
  J15 = female pin header, 36 pins [form="♀ (female)"]
  J16 = female pin header, 36 pins [form="♀ (female)"]
  J17 = female pin header, 36 pins [form="♀ (female)"]
  J18 = female pin header, 36 pins [form="♀ (female)"]
  J19 = female pin header, 36 pins [form="♀ (female)"]
  J20 = female pin header, 36 pins [form="♀ (female)"]
  J21 = female pin header, 36 pins [form="♀ (female)"]
  J22 = female pin header, 36 pins [form="♀ (female)"]
  J23 = female pin header, 36 pins [form="♀ (female)"]
  J24 = female pin header, 36 pins [form="♀ (female)"]
  J25 = female pin header, 36 pins [form="♀ (female)"]
  J26 = female pin header, 36 pins [form="♀ (female)"]
  J27 = female pin header, 36 pins [form="♀ (female)"]
  J28 = female pin header, 36 pins [form="♀ (female)"]
  J29 = female pin header, 36 pins [form="♀ (female)"]
  J30 = female pin header, 36 pins [form="♀ (female)"]
  J31 = female pin header, 36 pins [form="♀ (female)"]
  J32 = female pin header, 36 pins [form="♀ (female)"]
  J33 = female pin header, 36 pins [form="♀ (female)"]
  J34 = female pin header, 36 pins [form="♀ (female)"]
  J35 = female pin header, 36 pins [form="♀ (female)"]
  J36 = female pin header, 36 pins [form="♀ (female)"]
  Power_plug = Power plug
  J42 = female pin header, 4 pins [form="♀ (female)"]
  J44 = female pin header, 4 pins [form="♀ (female)"]
  J43 = female pin header, 4 pins [form="♀ (female)"]
  J45 = female pin header, 20 pins [form="♀ (female)"]
  J46 = female pin header, 20 pins [form="♀ (female)"]
  J47 = female pin header, 20 pins [form="♀ (female)"]
  J48 = female pin header, 20 pins [form="♀ (female)"]
  J38 = female pin header, 4 pins [form="♀ (female)"]
  J39 = female pin header, 4 pins [form="♀ (female)"]
  J40 = female pin header, 4 pins [form="♀ (female)"]

nets:
  N1: J4.pin1, J4.pin2, J4.pin3, J4.pin4, J4.pin5, J4.pin6, J4.pin7, J4.pin8, J4.pin9, J4.pin10, J4.pin11, J4.pin12, J4.pin13, J4.pin14, J4.pin15, J4.pin16, J4.pin17, J4.pin18, J4.pin19, J4.pin20, J4.pin21, J4.pin22, J4.pin23, J4.pin24, J4.pin25, J4.pin26, J4.pin27, J4.pin28, J4.pin29, J4.pin30, J4.pin31, J4.pin32, J4.pin33, J4.pin34, J4.pin35, J4.pin36
  N2: J5.pin1, J5.pin2, J5.pin3, J5.pin4, J5.pin5, J5.pin6, J5.pin7, J5.pin8, J5.pin9, J5.pin10, J5.pin11, J5.pin12, J5.pin13, J5.pin14, J5.pin15, J5.pin16, J5.pin17, J5.pin18, J5.pin19, J5.pin20, J5.pin21, J5.pin22, J5.pin23, J5.pin24, J5.pin25, J5.pin26, J5.pin27, J5.pin28, J5.pin29, J5.pin30, J5.pin31, J5.pin32, J5.pin33, J5.pin34, J5.pin35, J5.pin36
  N3: J13.pin1, J14.pin1, J15.pin1, J16.pin1, J17.pin1
  N4: J13.pin2, J14.pin2, J15.pin2, J16.pin2, J17.pin2
  N5: J13.pin3, J14.pin3, J15.pin3, J16.pin3, J17.pin3
  N6: J13.pin4, J14.pin4, J15.pin4, J16.pin4, J17.pin4
  N7: J13.pin5, J14.pin5, J15.pin5, J16.pin5, J17.pin5
  N8: J13.pin6, J14.pin6, J15.pin6, J16.pin6, J17.pin6
  N9: J13.pin7, J14.pin7, J15.pin7, J16.pin7, J17.pin7
  N10: J13.pin8, J14.pin8, J15.pin8, J16.pin8, J17.pin8
  N11: J13.pin9, J14.pin9, J15.pin9, J16.pin9, J17.pin9
  N12: J13.pin10, J14.pin10, J15.pin10, J16.pin10, J17.pin10
  N13: J13.pin11, J14.pin11, J15.pin11, J16.pin11, J17.pin11
  N14: J13.pin12, J14.pin12, J15.pin12, J16.pin12, J17.pin12
  N15: J13.pin13, J14.pin13, J15.pin13, J16.pin13, J17.pin13
  N16: J13.pin14, J14.pin14, J15.pin14, J16.pin14, J17.pin14
  N17: J13.pin15, J14.pin15, J15.pin15, J16.pin15, J17.pin15
  N18: J13.pin16, J14.pin16, J15.pin16, J16.pin16, J17.pin16
  N19: J13.pin17, J14.pin17, J15.pin17, J16.pin17, J17.pin17
  N20: J13.pin18, J14.pin18, J15.pin18, J16.pin18, J17.pin18
  N21: J13.pin19, J14.pin19, J15.pin19, J16.pin19, J17.pin19
  N22: J13.pin20, J14.pin20, J15.pin20, J16.pin20, J17.pin20
  N23: J13.pin21, J14.pin21, J15.pin21, J16.pin21, J17.pin21
  N24: J13.pin22, J14.pin22, J15.pin22, J16.pin22, J17.pin22
  N25: J13.pin23, J14.pin23, J15.pin23, J16.pin23, J17.pin23
  N26: J13.pin24, J14.pin24, J15.pin24, J16.pin24, J17.pin24
  N27: J13.pin25, J14.pin25, J15.pin25, J16.pin25, J17.pin25
  N28: J13.pin26, J14.pin26, J15.pin26, J16.pin26, J17.pin26
  N29: J13.pin27, J14.pin27, J15.pin27, J16.pin27, J17.pin27
  N30: J13.pin28, J14.pin28, J15.pin28, J16.pin28, J17.pin28
  N31: J13.pin29, J14.pin29, J15.pin29, J16.pin29, J17.pin29
  N32: J13.pin30, J14.pin30, J15.pin30, J16.pin30, J17.pin30
  N33: J13.pin31, J14.pin31, J15.pin31, J16.pin31, J17.pin31
  N34: J13.pin32, J14.pin32, J15.pin32, J16.pin32, J17.pin32
  N35: J13.pin33, J14.pin33, J15.pin33, J16.pin33, J17.pin33
  N36: J13.pin34, J14.pin34, J15.pin34, J16.pin34, J17.pin34
  N37: J13.pin35, J14.pin35, J15.pin35, J16.pin35, J17.pin35
  N38: J13.pin36, J14.pin36, J15.pin36, J16.pin36, J17.pin36
  N39: J18.pin1, J19.pin1, J20.pin1, J21.pin1, J22.pin1
  N40: J18.pin2, J19.pin2, J20.pin2, J21.pin2, J22.pin2
  N41: J18.pin3, J19.pin3, J20.pin3, J21.pin3, J22.pin3
  N42: J18.pin4, J19.pin4, J20.pin4, J21.pin4, J22.pin4
  N43: J18.pin5, J19.pin5, J20.pin5, J21.pin5, J22.pin5
  N44: J18.pin6, J19.pin6, J20.pin6, J21.pin6, J22.pin6
  N45: J18.pin7, J19.pin7, J20.pin7, J21.pin7, J22.pin7
  N46: J18.pin8, J19.pin8, J20.pin8, J21.pin8, J22.pin8
  N47: J18.pin9, J19.pin9, J20.pin9, J21.pin9, J22.pin9
  N48: J18.pin10, J19.pin10, J20.pin10, J21.pin10, J22.pin10
  N49: J18.pin11, J19.pin11, J20.pin11, J21.pin11, J22.pin11
  N50: J18.pin12, J19.pin12, J20.pin12, J21.pin12, J22.pin12
  N51: J18.pin13, J19.pin13, J20.pin13, J21.pin13, J22.pin13
  N52: J18.pin14, J19.pin14, J20.pin14, J21.pin14, J22.pin14
  N53: J18.pin15, J19.pin15, J20.pin15, J21.pin15, J22.pin15
  N54: J18.pin16, J19.pin16, J20.pin16, J21.pin16, J22.pin16
  N55: J18.pin17, J19.pin17, J20.pin17, J21.pin17, J22.pin17
  N56: J18.pin18, J19.pin18, J20.pin18, J21.pin18, J22.pin18
  N57: J18.pin19, J19.pin19, J20.pin19, J21.pin19, J22.pin19
  N58: J18.pin20, J19.pin20, J20.pin20, J21.pin20, J22.pin20
  N59: J18.pin21, J19.pin21, J20.pin21, J21.pin21, J22.pin21
  N60: J18.pin22, J19.pin22, J20.pin22, J21.pin22, J22.pin22
  N61: J18.pin23, J19.pin23, J20.pin23, J21.pin23, J22.pin23
  N62: J18.pin24, J19.pin24, J20.pin24, J21.pin24, J22.pin24
  N63: J18.pin25, J19.pin25, J20.pin25, J21.pin25, J22.pin25
  N64: J18.pin26, J19.pin26, J20.pin26, J21.pin26, J22.pin26
  N65: J18.pin27, J19.pin27, J20.pin27, J21.pin27, J22.pin27
  N66: J18.pin28, J19.pin28, J20.pin28, J21.pin28, J22.pin28
  N67: J18.pin29, J19.pin29, J20.pin29, J21.pin29, J22.pin29
  N68: J18.pin30, J19.pin30, J20.pin30, J21.pin30, J22.pin30
  N69: J18.pin31, J19.pin31, J20.pin31, J21.pin31, J22.pin31
  N70: J18.pin32, J19.pin32, J20.pin32, J21.pin32, J22.pin32
  N71: J18.pin33, J19.pin33, J20.pin33, J21.pin33, J22.pin33
  N72: J18.pin34, J19.pin34, J20.pin34, J21.pin34, J22.pin34
  N73: J18.pin35, J19.pin35, J20.pin35, J21.pin35, J22.pin35
  N74: J18.pin36, J19.pin36, J20.pin36, J21.pin36, J22.pin36
  N75: J23.pin1, J24.pin1, J25.pin1, J26.pin1, J27.pin1
  N76: J23.pin2, J24.pin2, J25.pin2, J26.pin2, J27.pin2
  N77: J23.pin3, J24.pin3, J25.pin3, J26.pin3, J27.pin3
  N78: J23.pin4, J24.pin4, J25.pin4, J26.pin4, J27.pin4
  N79: J23.pin5, J24.pin5, J25.pin5, J26.pin5, J27.pin5
  N80: J23.pin6, J24.pin6, J25.pin6, J26.pin6, J27.pin6
  N81: J23.pin7, J24.pin7, J25.pin7, J26.pin7, J27.pin7
  N82: J23.pin8, J24.pin8, J25.pin8, J26.pin8, J27.pin8
  N83: J23.pin9, J24.pin9, J25.pin9, J26.pin9, J27.pin9
  N84: J23.pin10, J24.pin10, J25.pin10, J26.pin10, J27.pin10
  N85: J23.pin11, J24.pin11, J25.pin11, J26.pin11, J27.pin11
  N86: J23.pin12, J24.pin12, J25.pin12, J26.pin12, J27.pin12
  N87: J23.pin13, J24.pin13, J25.pin13, J26.pin13, J27.pin13
  N88: J23.pin14, J24.pin14, J25.pin14, J26.pin14, J27.pin14
  N89: J23.pin15, J24.pin15, J25.pin15, J26.pin15, J27.pin15
  N90: J23.pin16, J24.pin16, J25.pin16, J26.pin16, J27.pin16
  N91: J23.pin17, J24.pin17, J25.pin17, J26.pin17, J27.pin17
  N92: J23.pin18, J24.pin18, J25.pin18, J26.pin18, J27.pin18
  N93: J23.pin19, J24.pin19, J25.pin19, J26.pin19, J27.pin19
  N94: J23.pin20, J24.pin20, J25.pin20, J26.pin20, J27.pin20
  N95: J23.pin21, J24.pin21, J25.pin21, J26.pin21, J27.pin21
  N96: J23.pin22, J24.pin22, J25.pin22, J26.pin22, J27.pin22
  N97: J23.pin23, J24.pin23, J25.pin23, J26.pin23, J27.pin23
  N98: J23.pin24, J24.pin24, J25.pin24, J26.pin24, J27.pin24
  N99: J23.pin25, J24.pin25, J25.pin25, J26.pin25, J27.pin25
  N100: J23.pin26, J24.pin26, J25.pin26, J26.pin26, J27.pin26
  N101: J23.pin27, J24.pin27, J25.pin27, J26.pin27, J27.pin27
  N102: J23.pin28, J24.pin28, J25.pin28, J26.pin28, J27.pin28
  N103: J23.pin29, J24.pin29, J25.pin29, J26.pin29, J27.pin29
  N104: J23.pin30, J24.pin30, J25.pin30, J26.pin30, J27.pin30
  N105: J23.pin31, J24.pin31, J25.pin31, J26.pin31, J27.pin31
  N106: J23.pin32, J24.pin32, J25.pin32, J26.pin32, J27.pin32
  N107: J23.pin33, J24.pin33, J25.pin33, J26.pin33, J27.pin33
  N108: J23.pin34, J24.pin34, J25.pin34, J26.pin34, J27.pin34
  N109: J23.pin35, J24.pin35, J25.pin35, J26.pin35, J27.pin35
  N110: J23.pin36, J24.pin36, J25.pin36, J26.pin36, J27.pin36
  N111: J28.pin1, J28.pin2, J28.pin3, J28.pin4, J28.pin5, J28.pin6, J28.pin7, J28.pin8, J28.pin9, J28.pin10, J28.pin11, J28.pin12, J28.pin13, J28.pin14, J28.pin15, J28.pin16, J28.pin17, J28.pin18, J28.pin19, J28.pin20, J28.pin21, J28.pin22, J28.pin23, J28.pin24, J28.pin25, J28.pin26, J28.pin27, J28.pin28, J28.pin29, J28.pin30, J28.pin31, J28.pin32, J28.pin33, J28.pin34, J28.pin35, J28.pin36
  N112: J29.pin1, J29.pin2, J29.pin3, J29.pin4, J29.pin5, J29.pin6, J29.pin7, J29.pin8, J29.pin9, J29.pin10, J29.pin11, J29.pin12, J29.pin13, J29.pin14, J29.pin15, J29.pin16, J29.pin17, J29.pin18, J29.pin19, J29.pin20, J29.pin21, J29.pin22, J29.pin23, J29.pin24, J29.pin25, J29.pin26, J29.pin27, J29.pin28, J29.pin29, J29.pin30, J29.pin31, J29.pin32, J29.pin33, J29.pin34, J29.pin35, J29.pin36
  N113: J30.pin1, J31.pin1, J32.pin1, J33.pin1, J34.pin1
  N114: J30.pin2, J31.pin2, J32.pin2, J33.pin2, J34.pin2
  N115: J30.pin3, J31.pin3, J32.pin3, J33.pin3, J34.pin3
  N116: J30.pin4, J31.pin4, J32.pin4, J33.pin4, J34.pin4
  N117: J30.pin5, J31.pin5, J32.pin5, J33.pin5, J34.pin5
  N118: J30.pin6, J31.pin6, J32.pin6, J33.pin6, J34.pin6
  N119: J30.pin7, J31.pin7, J32.pin7, J33.pin7, J34.pin7
  N120: J30.pin8, J31.pin8, J32.pin8, J33.pin8, J34.pin8
  N121: J30.pin9, J31.pin9, J32.pin9, J33.pin9, J34.pin9
  N122: J30.pin10, J31.pin10, J32.pin10, J33.pin10, J34.pin10
  N123: J30.pin11, J31.pin11, J32.pin11, J33.pin11, J34.pin11
  N124: J30.pin12, J31.pin12, J32.pin12, J33.pin12, J34.pin12
  N125: J30.pin13, J31.pin13, J32.pin13, J33.pin13, J34.pin13
  N126: J30.pin14, J31.pin14, J32.pin14, J33.pin14, J34.pin14
  N127: J30.pin15, J31.pin15, J32.pin15, J33.pin15, J34.pin15
  N128: J30.pin16, J31.pin16, J32.pin16, J33.pin16, J34.pin16
  N129: J30.pin17, J31.pin17, J32.pin17, J33.pin17, J34.pin17
  N130: J30.pin18, J31.pin18, J32.pin18, J33.pin18, J34.pin18
  N131: J30.pin19, J31.pin19, J32.pin19, J33.pin19, J34.pin19
  N132: J30.pin20, J31.pin20, J32.pin20, J33.pin20, J34.pin20
  N133: J30.pin21, J31.pin21, J32.pin21, J33.pin21, J34.pin21
  N134: J30.pin22, J31.pin22, J32.pin22, J33.pin22, J34.pin22
  N135: J30.pin23, J31.pin23, J32.pin23, J33.pin23, J34.pin23
  N136: J30.pin24, J31.pin24, J32.pin24, J33.pin24, J34.pin24
  N137: J30.pin25, J31.pin25, J32.pin25, J33.pin25, J34.pin25
  N138: J30.pin26, J31.pin26, J32.pin26, J33.pin26, J34.pin26
  N139: J30.pin27, J31.pin27, J32.pin27, J33.pin27, J34.pin27
  N140: J30.pin28, J31.pin28, J32.pin28, J33.pin28, J34.pin28
  N141: J30.pin29, J31.pin29, J32.pin29, J33.pin29, J34.pin29
  N142: J30.pin30, J31.pin30, J32.pin30, J33.pin30, J34.pin30
  N143: J30.pin31, J31.pin31, J32.pin31, J33.pin31, J34.pin31
  N144: J30.pin32, J31.pin32, J32.pin32, J33.pin32, J34.pin32
  N145: J30.pin33, J31.pin33, J32.pin33, J33.pin33, J34.pin33
  N146: J30.pin34, J31.pin34, J32.pin34, J33.pin34, J34.pin34
  N147: J30.pin35, J31.pin35, J32.pin35, J33.pin35, J34.pin35
  N148: J30.pin36, J31.pin36, J32.pin36, J33.pin36, J34.pin36
  N149: J35.pin1, J35.pin2, J35.pin3, J35.pin4, J35.pin5, J35.pin6, J35.pin7, J35.pin8, J35.pin9, J35.pin10, J35.pin11, J35.pin12, J35.pin13, J35.pin14, J35.pin15, J35.pin16, J35.pin17, J35.pin18, J35.pin19, J35.pin20, J35.pin21, J35.pin22, J35.pin23, J35.pin24, J35.pin25, J35.pin26, J35.pin27, J35.pin28, J35.pin29, J35.pin30, J35.pin31, J35.pin32, J35.pin33, J35.pin34, J35.pin35, J35.pin36
  N150: J36.pin1, J36.pin2, J36.pin3, J36.pin4, J36.pin5, J36.pin6, J36.pin7, J36.pin8, J36.pin9, J36.pin10, J36.pin11, J36.pin12, J36.pin13, J36.pin14, J36.pin15, J36.pin16, J36.pin17, J36.pin18, J36.pin19, J36.pin20, J36.pin21, J36.pin22, J36.pin23, J36.pin24, J36.pin25, J36.pin26, J36.pin27, J36.pin28, J36.pin29, J36.pin30, J36.pin31, J36.pin32, J36.pin33, J36.pin34, J36.pin35, J36.pin36
  N151: Power_plug.GND, J42.pin1, J42.pin2, J42.pin3, J42.pin4, J43.pin1, J43.pin2, J43.pin3, J43.pin4, J38.pin1, J38.pin2, J38.pin3, J38.pin4, J39.pin1, J39.pin2, J39.pin3, J39.pin4
  N152: Power_plug.VCC, J44.pin1, J44.pin2, J44.pin3, J44.pin4, J40.pin1, J40.pin2, J40.pin3, J40.pin4
  N153: J45.pin1, J45.pin2, J45.pin3, J45.pin4
  N154: J45.pin5, J46.pin5, J47.pin5, J48.pin5
  N155: J45.pin6, J46.pin6, J47.pin6, J48.pin6
  N156: J45.pin7, J46.pin7, J47.pin7, J48.pin7
  N157: J45.pin8, J46.pin8, J47.pin8, J48.pin8
  N158: J45.pin9, J45.pin10, J45.pin11, J45.pin12
  N159: J45.pin13, J46.pin13, J47.pin13, J48.pin13
  N160: J45.pin14, J46.pin14, J47.pin14, J48.pin14
  N161: J45.pin15, J46.pin15, J47.pin15, J48.pin15
  N162: J45.pin16, J46.pin16, J47.pin16, J48.pin16
  N163: J45.pin17, J45.pin18, J45.pin19, J45.pin20
  N164: J46.pin1, J46.pin2, J46.pin3, J46.pin4
  N165: J46.pin9, J46.pin10, J46.pin11, J46.pin12
  N166: J46.pin17, J46.pin18, J46.pin19, J46.pin20
  N167: J47.pin1, J47.pin2, J47.pin3, J47.pin4
  N168: J47.pin9, J47.pin10, J47.pin11, J47.pin12
  N169: J47.pin17, J47.pin18, J47.pin19, J47.pin20
  N170: J48.pin1, J48.pin2, J48.pin3, J48.pin4
  N171: J48.pin9, J48.pin10, J48.pin11, J48.pin12
  N172: J48.pin17, J48.pin18, J48.pin19, J48.pin20

notes:
  -
  +
  a
  b
  c
  d
  e
  01
  02
  03
  04
  05
  06
  07
  08
  09
  12
  10
  11
  13
  14
  22
  23
  19
  15
  24
  16
  21
  17
  20
  18
  25
  26
  34
  35
  31
  27
  36
  28
  33
  29
  32
  30
  BB2636PP0420
  UniversalPCB
