# Fritzing sketch bb3614 (saved by Fritzing 0.9.3b)
circuit board: 10cm x 5cm
breadboards: 1

parts:
  J23 = female pin header, 36 pins [form="♀ (female)"]
  J24 = female pin header, 36 pins [form="♀ (female)"]
  J25 = female pin header, 36 pins [form="♀ (female)"]
  J26 = female pin header, 36 pins [form="♀ (female)"]
  J27 = female pin header, 36 pins [form="♀ (female)"]
  J28 = female pin header, 36 pins [form="♀ (female)"]
  J29 = female pin header, 36 pins [form="♀ (female)"]
  J30 = female pin header, 36 pins [form="♀ (female)"]
  J31 = female pin header, 36 pins [form="♀ (female)"]
  J32 = female pin header, 36 pins [form="♀ (female)"]
  J33 = female pin header, 36 pins [form="♀ (female)"]
  J34 = female pin header, 36 pins [form="♀ (female)"]
  J35 = female pin header, 36 pins [form="♀ (female)"]
  J36 = female pin header, 36 pins [form="♀ (female)"]
  J37 = female pin header, 36 pins [form="♀ (female)"]
  J38 = female pin header, 36 pins [form="♀ (female)"]

nets:
  N1: J23.pin1, J24.pin1, J25.pin1, J26.pin1, J27.pin1, J38.pin1
  N2: J23.pin2, J24.pin2, J25.pin2, J26.pin2, J27.pin2, J38.pin2
  N3: J23.pin3, J24.pin3, J25.pin3, J26.pin3, J27.pin3, J38.pin3
  N4: J23.pin4, J24.pin4, J25.pin4, J26.pin4, J27.pin4, J38.pin4
  N5: J23.pin5, J24.pin5, J25.pin5, J26.pin5, J27.pin5, J38.pin5
  N6: J23.pin6, J24.pin6, J25.pin6, J26.pin6, J27.pin6, J38.pin6
  N7: J23.pin7, J24.pin7, J25.pin7, J26.pin7, J27.pin7, J38.pin7
  N8: J23.pin8, J24.pin8, J25.pin8, J26.pin8, J27.pin8, J38.pin8
  N9: J23.pin9, J24.pin9, J25.pin9, J26.pin9, J27.pin9, J38.pin9
  N10: J23.pin10, J24.pin10, J25.pin10, J26.pin10, J27.pin10, J38.pin10
  N11: J23.pin11, J24.pin11, J25.pin11, J26.pin11, J27.pin11, J38.pin11
  N12: J23.pin12, J24.pin12, J25.pin12, J26.pin12, J27.pin12, J38.pin12
  N13: J23.pin13, J24.pin13, J25.pin13, J26.pin13, J27.pin13, J38.pin13
  N14: J23.pin14, J24.pin14, J25.pin14, J26.pin14, J27.pin14, J38.pin14
  N15: J23.pin15, J24.pin15, J25.pin15, J26.pin15, J27.pin15, J38.pin15
  N16: J23.pin16, J24.pin16, J25.pin16, J26.pin16, J27.pin16, J38.pin16
  N17: J23.pin17, J24.pin17, J25.pin17, J26.pin17, J27.pin17, J38.pin17
  N18: J23.pin18, J24.pin18, J25.pin18, J26.pin18, J27.pin18, J38.pin18
  N19: J23.pin19, J24.pin19, J25.pin19, J26.pin19, J27.pin19, J38.pin19
  N20: J23.pin20, J24.pin20, J25.pin20, J26.pin20, J27.pin20, J38.pin20
  N21: J23.pin21, J24.pin21, J25.pin21, J26.pin21, J27.pin21, J38.pin21
  N22: J23.pin22, J24.pin22, J25.pin22, J26.pin22, J27.pin22, J38.pin22
  N23: J23.pin23, J24.pin23, J25.pin23, J26.pin23, J27.pin23, J38.pin23
  N24: J23.pin24, J24.pin24, J25.pin24, J26.pin24, J27.pin24, J38.pin24
  N25: J23.pin25, J24.pin25, J25.pin25, J26.pin25, J27.pin25, J38.pin25
  N26: J23.pin26, J24.pin26, J25.pin26, J26.pin26, J27.pin26, J38.pin26
  N27: J23.pin27, J24.pin27, J25.pin27, J26.pin27, J27.pin27, J38.pin27
  N28: J23.pin28, J24.pin28, J25.pin28, J26.pin28, J27.pin28, J38.pin28
  N29: J23.pin29, J24.pin29, J25.pin29, J26.pin29, J27.pin29, J38.pin29
  N30: J23.pin30, J24.pin30, J25.pin30, J26.pin30, J27.pin30, J38.pin30
  N31: J23.pin31, J24.pin31, J25.pin31, J26.pin31, J27.pin31, J38.pin31
  N32: J23.pin32, J24.pin32, J25.pin32, J26.pin32, J27.pin32, J38.pin32
  N33: J23.pin33, J24.pin33, J25.pin33, J26.pin33, J27.pin33, J38.pin33
  N34: J23.pin34, J24.pin34, J25.pin34, J26.pin34, J27.pin34, J38.pin34
  N35: J23.pin35, J24.pin35, J25.pin35, J26.pin35, J27.pin35, J38.pin35
  N36: J23.pin36, J24.pin36, J25.pin36, J26.pin36, J27.pin36, J38.pin36
  N37: J28.pin1, J28.pin2, J28.pin3, J28.pin4, J28.pin5, J28.pin6, J28.pin7, J28.pin8, J28.pin9, J28.pin10, J28.pin11, J28.pin12, J28.pin13, J28.pin14, J28.pin15, J28.pin16, J28.pin17, J28.pin18, J28.pin19, J28.pin20, J28.pin21, J28.pin22, J28.pin23, J28.pin24, J28.pin25, J28.pin26, J28.pin27, J28.pin28, J28.pin29, J28.pin30, J28.pin31, J28.pin32, J28.pin33, J28.pin34, J28.pin35, J28.pin36
  N38: J29.pin1, J29.pin2, J29.pin3, J29.pin4, J29.pin5, J29.pin6, J29.pin7, J29.pin8, J29.pin9, J29.pin10, J29.pin11, J29.pin12, J29.pin13, J29.pin14, J29.pin15, J29.pin16, J29.pin17, J29.pin18, J29.pin19, J29.pin20, J29.pin21, J29.pin22, J29.pin23, J29.pin24, J29.pin25, J29.pin26, J29.pin27, J29.pin28, J29.pin29, J29.pin30, J29.pin31, J29.pin32, J29.pin33, J29.pin34, J29.pin35, J29.pin36
  N39: J30.pin1, J31.pin1, J32.pin1, J33.pin1, J34.pin1, J37.pin1
  N40: J30.pin2, J31.pin2, J32.pin2, J33.pin2, J34.pin2, J37.pin2
  N41: J30.pin3, J31.pin3, J32.pin3, J33.pin3, J34.pin3, J37.pin3
  N42: J30.pin4, J31.pin4, J32.pin4, J33.pin4, J34.pin4, J37.pin4
  N43: J30.pin5, J31.pin5, J32.pin5, J33.pin5, J34.pin5, J37.pin5
  N44: J30.pin6, J31.pin6, J32.pin6, J33.pin6, J34.pin6, J37.pin6
  N45: J30.pin7, J31.pin7, J32.pin7, J33.pin7, J34.pin7, J37.pin7
  N46: J30.pin8, J31.pin8, J32.pin8, J33.pin8, J34.pin8, J37.pin8
  N47: J30.pin9, J31.pin9, J32.pin9, J33.pin9, J34.pin9, J37.pin9
  N48: J30.pin10, J31.pin10, J32.pin10, J33.pin10, J34.pin10, J37.pin10
  N49: J30.pin11, J31.pin11, J32.pin11, J33.pin11, J34.pin11, J37.pin11
  N50: J30.pin12, J31.pin12, J32.pin12, J33.pin12, J34.pin12, J37.pin12
  N51: J30.pin13, J31.pin13, J32.pin13, J33.pin13, J34.pin13, J37.pin13
  N52: J30.pin14, J31.pin14, J32.pin14, J33.pin14, J34.pin14, J37.pin14
  N53: J30.pin15, J31.pin15, J32.pin15, J33.pin15, J34.pin15, J37.pin15
  N54: J30.pin16, J31.pin16, J32.pin16, J33.pin16, J34.pin16, J37.pin16
  N55: J30.pin17, J31.pin17, J32.pin17, J33.pin17, J34.pin17, J37.pin17
  N56: J30.pin18, J31.pin18, J32.pin18, J33.pin18, J34.pin18, J37.pin18
  N57: J30.pin19, J31.pin19, J32.pin19, J33.pin19, J34.pin19, J37.pin19
  N58: J30.pin20, J31.pin20, J32.pin20, J33.pin20, J34.pin20, J37.pin20
  N59: J30.pin21, J31.pin21, J32.pin21, J33.pin21, J34.pin21, J37.pin21
  N60: J30.pin22, J31.pin22, J32.pin22, J33.pin22, J34.pin22, J37.pin22
  N61: J30.pin23, J31.pin23, J32.pin23, J33.pin23, J34.pin23, J37.pin23
  N62: J30.pin24, J31.pin24, J32.pin24, J33.pin24, J34.pin24, J37.pin24
  N63: J30.pin25, J31.pin25, J32.pin25, J33.pin25, J34.pin25, J37.pin25
  N64: J30.pin26, J31.pin26, J32.pin26, J33.pin26, J34.pin26, J37.pin26
  N65: J30.pin27, J31.pin27, J32.pin27, J33.pin27, J34.pin27, J37.pin27
  N66: J30.pin28, J31.pin28, J32.pin28, J33.pin28, J34.pin28, J37.pin28
  N67: J30.pin29, J31.pin29, J32.pin29, J33.pin29, J34.pin29, J37.pin29
  N68: J30.pin30, J31.pin30, J32.pin30, J33.pin30, J34.pin30, J37.pin30
  N69: J30.pin31, J31.pin31, J32.pin31, J33.pin31, J34.pin31, J37.pin31
  N70: J30.pin32, J31.pin32, J32.pin32, J33.pin32, J34.pin32, J37.pin32
  N71: J30.pin33, J31.pin33, J32.pin33, J33.pin33, J34.pin33, J37.pin33
  N72: J30.pin34, J31.pin34, J32.pin34, J33.pin34, J34.pin34, J37.pin34
  N73: J30.pin35, J31.pin35, J32.pin35, J33.pin35, J34.pin35, J37.pin35
  N74: J30.pin36, J31.pin36, J32.pin36, J33.pin36, J34.pin36, J37.pin36
  N75: J35.pin1, J35.pin2, J35.pin3, J35.pin4, J35.pin5, J35.pin6, J35.pin7, J35.pin8, J35.pin9, J35.pin10, J35.pin11, J35.pin12, J35.pin13, J35.pin14, J35.pin15, J35.pin16, J35.pin17, J35.pin18, J35.pin19, J35.pin20, J35.pin21, J35.pin22, J35.pin23, J35.pin24, J35.pin25, J35.pin26, J35.pin27, J35.pin28, J35.pin29, J35.pin30, J35.pin31, J35.pin32, J35.pin33, J35.pin34, J35.pin35, J35.pin36
  N76: J36.pin1, J36.pin2, J36.pin3, J36.pin4, J36.pin5, J36.pin6, J36.pin7, J36.pin8, J36.pin9, J36.pin10, J36.pin11, J36.pin12, J36.pin13, J36.pin14, J36.pin15, J36.pin16, J36.pin17, J36.pin18, J36.pin19, J36.pin20, J36.pin21, J36.pin22, J36.pin23, J36.pin24, J36.pin25, J36.pin26, J36.pin27, J36.pin28, J36.pin29, J36.pin30, J36.pin31, J36.pin32, J36.pin33, J36.pin34, J36.pin35, J36.pin36

notes:
  -
  +
  a
  b
  c
  d
  e
  01
  02
  03
  04
  05
  06
  07
  08
  09
  12
  10
  11
  13
  14
  22
  23
  19
  15
  24
  16
  21
  17
  20
  18
  25
  26
  34
  35
  31
  27
  36
  28
  33
  29
  32
  30
  BB3614
  UniversalPCB
  f
